// Logisim project final exam.circ as structural Verilog: 1 circuit, main circuit main
module main (
  output QA,
  output QA_prime,
  output QB,
  output QB_prime,
  output QC,
  output QC_prime,
  output QD,
  output QD_prime
);

  wire and_1_out, clock_1_out, or_1_out;

  and and_1 (and_1_out, QA_prime, QD);
  or or_1 (or_1_out, QA, QC_prime);
  Clock clock_1 (.out(clock_1_out));
  J_K_Flip_Flop j_k_ff_1 (.J(QB), .clk(clock_1_out), .K(QD), .Q(QA), .Qn(QA_prime));  // open: preset, en, reset
  J_K_Flip_Flop j_k_ff_2 (
    .J(and_1_out), .clk(clock_1_out), .K(1'b1), .Q(QB), .Qn(QB_prime));  // open: preset, en, reset
  J_K_Flip_Flop j_k_ff_3 (.J(QB_prime), .clk(clock_1_out), .K(1'b1), .Q(QC), .Qn(QC_prime));  // open: preset, en, reset
  J_K_Flip_Flop j_k_ff_4 (.J(1'b1), .clk(clock_1_out), .K(or_1_out), .Q(QD), .Qn(QD_prime));  // open: preset, en, reset
endmodule
