// Logisim project lab 1.circ as structural Verilog: 3 circuits, main circuit 1
module _1 (
  input  X,
  input  Y,
  input  Z,
  output F
);

  wire and_1_out, and_2_out, not_1_out, not_2_out;

  not not_1 (not_1_out, X);
  not not_2 (not_2_out, Y);
  and and_1 (and_1_out, not_1_out, not_2_out);
  and and_2 (and_2_out, Y, Z);
  or or_1 (F, and_1_out, and_2_out);
endmodule

module _2 (
  input  X,
  input  Y,
  input  Z,
  output F
);

  wire and_1_out, and_2_out, and_3_out, not_1_out;

  not not_1 (not_1_out, Z);
  and and_1 (and_1_out, X, Y);
  and and_2 (and_2_out, X, not_1_out);
  and and_3 (and_3_out, X, Y, Z);
  or or_1 (F, and_1_out, and_2_out, and_3_out);
endmodule

module _3 (
  input  X,
  input  Y,
  input  Z,
  output F
);

  wire and_1_out, and_2_out, and_3_out, not_1_out, not_2_out;

  not not_1 (not_1_out, Y);
  not not_2 (not_2_out, X);
  and and_1 (and_1_out, X, Z);
  and and_2 (and_2_out, X, not_1_out);
  and and_3 (and_3_out, not_2_out, Y, Z);
  or or_1 (F, and_1_out, and_2_out, and_3_out);
endmodule
