// Logisim project lab 10.circ as structural Verilog: 4 circuits, main circuit 1
module _1 (
  input  X,
  input  Y,
  output Q1,
  output Q1_prime,
  output Q0,
  output Q0_prime,
  output F
);

  wire and_1_out, and_2_out, clock_1_out, or_1_out;

  and and_1 (and_1_out, X, Y);
  and and_2 (and_2_out, X, Q1_prime);
  Clock clock_1 (.out(clock_1_out));
  or or_1 (or_1_out, and_1_out, and_2_out);
  D_Flip_Flop d_ff_1 (.clk(clock_1_out), .D(or_1_out), .Q(Q1), .Qn(Q1_prime));  // open: preset, en, reset
  D_Flip_Flop d_ff_2 (.clk(clock_1_out), .D(and_2_out), .Q(Q0), .Qn(Q0_prime));  // open: preset, en, reset
  xor xor_1 (F, Q0, Y);
endmodule

module _2 (
  input  [1:0] S0S1,
  input  A,
  input  B,
  input  C,
  output QA,
  output QA_prime,
  output QB,
  output QB_prime,
  output QC,
  output QC_prime
);

  wire clock_1_out, multiplexer_1_out, multiplexer_2_out, multiplexer_3_out;

  Multiplexer #(.select(2), .enable("false")) multiplexer_1 (
    .in0(QA), .in1(QA_prime), .in2(1'b0), .in3(A), .out(multiplexer_1_out), .sel(S0S1));
  Multiplexer #(.select(2), .enable("false")) multiplexer_2 (
    .in0(QB), .in1(QB_prime), .in2(1'b0), .in3(B), .out(multiplexer_2_out), .sel(S0S1));
  Multiplexer #(.select(2), .enable("false")) multiplexer_3 (
    .in0(QC), .in1(QC_prime), .in2(1'b0), .in3(C), .out(multiplexer_3_out), .sel(S0S1));
  Clock clock_1 (.out(clock_1_out));
  D_Flip_Flop d_ff_1 (.clk(clock_1_out), .D(multiplexer_1_out), .Q(QA), .Qn(QA_prime));  // open: preset, en, reset
  D_Flip_Flop d_ff_2 (.clk(clock_1_out), .D(multiplexer_2_out), .Q(QB), .Qn(QB_prime));  // open: preset, en, reset
  D_Flip_Flop d_ff_3 (.clk(clock_1_out), .D(multiplexer_3_out), .Q(QC), .Qn(QC_prime));  // open: preset, en, reset
endmodule

module _3 (
  input  A,
  input  B,
  input  C,
  input  [1:0] S1S0,
  output QA,
  output QA_prime,
  output QB,
  output QB_prime,
  output QC,
  output QC_prime
);

  wire and_1_out, and_2_out, and_3_out, and_4_out, and_5_out, and_6_out, and_7_out, clock_1_out,
       decoder_1_out0, decoder_1_out1, decoder_1_out2, decoder_1_out3, not_1_out, or_1_out, or_2_out,
       or_3_out;

  Decoder #(.select(2), .enable("false")) decoder_1 (
    .out0(decoder_1_out0), .out1(decoder_1_out1), .out2(decoder_1_out2), .out3(decoder_1_out3), .sel(S1S0));
  and and_1 (and_1_out, A, decoder_1_out3);
  and and_2 (and_2_out, decoder_1_out1, QA_prime);
  and and_3 (and_3_out, B, decoder_1_out3);
  and and_4 (and_4_out, decoder_1_out1, QB_prime);
  and and_5 (and_5_out, C, decoder_1_out3);
  and and_6 (and_6_out, decoder_1_out1, QC_prime);
  not not_1 (not_1_out, decoder_1_out0);
  or or_1 (or_1_out, and_1_out, and_2_out);
  or or_2 (or_2_out, and_3_out, and_4_out);
  or or_3 (or_3_out, and_5_out, and_6_out);
  and and_7 (and_7_out, not_1_out, clock_1_out);
  Clock clock_1 (.out(clock_1_out));
  D_Flip_Flop d_ff_1 (
    .clk(and_7_out), .D(or_1_out), .Q(QA), .Qn(QA_prime), .reset(decoder_1_out2));  // open: preset, en
  D_Flip_Flop d_ff_2 (
    .clk(and_7_out), .D(or_2_out), .Q(QB), .Qn(QB_prime), .reset(decoder_1_out2));  // open: preset, en
  D_Flip_Flop d_ff_3 (
    .clk(and_7_out), .D(or_3_out), .Q(QC), .Qn(QC_prime), .reset(decoder_1_out2));  // open: preset, en
endmodule

module _4 (
  input  X,
  output Z,
  output QA,
  output QA_prime,
  output QB,
  output QB_prime,
  output QC,
  output QC_prime
);

  wire and_1_out, and_2_out, and_3_out, and_4_out, and_5_out, and_6_out, clock_1_out, not_1_out, not_2_out,
       not_3_out, or_1_out, or_2_out, or_3_out;

  not not_1 (not_1_out, X);
  not not_2 (not_2_out, X);
  not not_3 (not_3_out, X);
  and and_1 (and_1_out, not_1_out, QB, QC);
  and and_2 (and_2_out, not_2_out, QB);
  and and_3 (and_3_out, X, QC);
  and and_4 (and_4_out, X, QA);
  and and_5 (and_5_out, X, QC);
  and and_6 (and_6_out, not_3_out, QC_prime);
  or or_1 (or_1_out, and_1_out, QA);
  or or_2 (or_2_out, and_2_out, and_3_out, and_4_out);
  or or_3 (or_3_out, and_5_out, and_6_out, QB);
  Clock clock_1 (.out(clock_1_out));
  T_Flip_Flop t_ff_1 (.clk(clock_1_out), .T(or_1_out), .Q(QA), .Qn(QA_prime));  // open: preset, reset, en
  T_Flip_Flop t_ff_2 (.clk(clock_1_out), .T(or_2_out), .Q(QB), .Qn(QB_prime));  // open: preset, reset, en
  T_Flip_Flop t_ff_3 (.clk(clock_1_out), .T(or_3_out), .Q(QC), .Qn(QC_prime));  // open: preset, reset, en

  assign Z = QA;
endmodule
