// Logisim project lab 2.circ as structural Verilog: 3 circuits, main circuit 1
module _1 (
  input  A,
  input  B,
  input  C,
  input  D,
  output X,
  output Y,
  output Z,
  output W
);

  wire and_1_out, nand_1_out, not_1_out;

  not not_1 (not_1_out, B);
  nand nand_1 (nand_1_out, C, D);
  and and_1 (and_1_out, not_1_out, nand_1_out);
  xor xor_1 (X, A, and_1_out);
  xor xor_2 (Y, B, nand_1_out);
  xor xor_3 (Z, C, D);
  xor xor_4 (W, D, 1'b1);
endmodule

module _2 (
  input  A,
  input  B,
  input  C,
  input  D,
  output X,
  output Y,
  output Z,
  output W
);

  wire and_1_out, and_2_out, and_3_out, and_4_out, not_1_out, not_2_out, not_3_out, or_1_out;

  or or_1 (or_1_out, C, D);
  not not_1 (not_1_out, C);
  not not_2 (not_2_out, D);
  not not_3 (not_3_out, B);
  and and_1 (and_1_out, not_1_out, not_2_out);
  and and_2 (and_2_out, B, or_1_out);
  and and_3 (and_3_out, not_3_out, or_1_out);
  and and_4 (and_4_out, B, and_1_out);
  or or_2 (X, A, and_2_out);
  or or_3 (Y, and_3_out, and_4_out);
  xor xor_1 (Z, C, D);

  assign W = D;
endmodule

module _3 (
  input  A,
  input  B,
  input  C,
  input  D,
  output W,
  output X,
  output Y,
  output Z
);

  wire and_1_out, and_2_out, and_3_out, and_4_out, not_1_out, not_2_out, or_1_out;

  not not_1 (not_1_out, B);
  or or_1 (or_1_out, C, D);
  not not_2 (not_2_out, or_1_out);
  and and_1 (and_1_out, C, D);
  and and_2 (and_2_out, or_1_out, B);
  and and_3 (and_3_out, not_1_out, or_1_out);
  not not_3 (Z, D);
  and and_4 (and_4_out, B, not_2_out);
  or or_2 (Y, not_2_out, and_1_out);
  or or_3 (W, A, and_2_out);
  or or_4 (X, and_3_out, and_4_out);
endmodule
