// Logisim project lab 3.circ as structural Verilog: 3 circuits, main circuit 1
module _1 (
  input  X,
  input  Y,
  input  Cin,
  output S,
  output Cout
);

  wire and_1_out, and_2_out, and_3_out, xor_1_out;

  xor xor_1 (xor_1_out, X, Y);
  and and_1 (and_1_out, X, Y);
  and and_2 (and_2_out, X, Cin);
  and and_3 (and_3_out, Y, Cin);
  xor xor_2 (S, xor_1_out, Cin);
  or or_1 (Cout, and_1_out, and_2_out, and_3_out);
endmodule

module _2 (
  input  A,
  input  B,
  input  C,
  input  D,
  output W,
  output X,
  output Y,
  output Z
);

  wire or_1_out, or_2_out;

  or or_1 (or_1_out, B, C, D);
  or or_2 (or_2_out, C, D);
  xor xor_1 (W, A, or_1_out);
  xor xor_2 (X, B, or_2_out);
  xor xor_3 (Y, C, D);

  assign Z = D;
endmodule

module _3 (
  input  A,
  input  B,
  input  C,
  input  D,
  output W,
  output X,
  output Y,
  output Z
);

  xor xor_1 (X, A, B);
  xor xor_2 (Y, X, C);
  xor xor_3 (Z, Y, D);

  assign W = A;
endmodule
