// Logisim project lab 4.circ as structural Verilog: 6 circuits, main circuit 2a
module _2a (
  input  X,
  input  Y,
  input  Z,
  output out_4
);

  wire nand_1_out, nand_2_out, nand_3_out, nand_4_out, nand_5_out, nand_6_out, nand_7_out, nand_8_out;

  nand nand_1 (nand_1_out, X, Y);
  nand nand_2 (nand_2_out, Z, Z);
  nand nand_3 (nand_3_out, nand_1_out, nand_1_out);
  nand nand_4 (nand_4_out, Y, nand_2_out);
  nand nand_5 (nand_5_out, X, nand_2_out);
  nand nand_6 (nand_6_out, nand_3_out, Z);
  nand nand_7 (nand_7_out, nand_6_out, nand_4_out);
  nand nand_8 (nand_8_out, nand_7_out, nand_7_out);
  nand nand_9 (out_4, nand_8_out, nand_5_out);
endmodule

module _2b (
  input  A,
  input  B,
  input  C,
  output G
);

  wire nand_1_out, nand_2_out, nand_3_out, nand_4_out, nand_5_out;

  nand nand_1 (nand_1_out, A, A);
  nand nand_2 (nand_2_out, C, C);
  nand nand_3 (nand_3_out, nand_1_out, C);
  nand nand_4 (nand_4_out, B, nand_2_out);
  nand nand_5 (nand_5_out, nand_3_out, nand_4_out);
  nand nand_6 (G, nand_5_out, nand_5_out);
endmodule

module _3a (
  input  A,
  input  B,
  input  C,
  output F
);

  wire nor_1_out, nor_2_out, nor_3_out;

  nor nor_1 (nor_1_out, A, A);
  nor nor_2 (nor_2_out, A, B);
  nor nor_3 (nor_3_out, nor_1_out, C);
  nor nor_4 (F, nor_2_out, nor_3_out);
endmodule

module _3b (
  input  X,
  input  Y,
  input  Z,
  output G
);

  wire nor_1_out, nor_2_out, nor_3_out, nor_4_out, nor_5_out, nor_6_out;

  nor nor_1 (nor_1_out, X, X);
  nor nor_2 (nor_2_out, Y, Y);
  nor nor_3 (nor_3_out, Z, Z);
  nor nor_4 (nor_4_out, nor_1_out, nor_3_out);
  nor nor_5 (nor_5_out, nor_2_out, Z);
  nor nor_6 (nor_6_out, nor_4_out, nor_5_out);
  nor nor_7 (G, nor_6_out, nor_6_out);
endmodule

module _4 (
  input  X,
  input  Y,
  input  Z,
  output F
);

  wire nand_1_out, nand_2_out, nand_3_out, nand_4_out, nand_5_out;

  nand nand_1 (nand_1_out, X, X);
  nand nand_2 (nand_2_out, Y, Y);
  nand nand_3 (nand_3_out, Z, Z);
  nand nand_4 (nand_4_out, nand_1_out, nand_2_out);
  nand nand_5 (nand_5_out, nand_4_out, nand_4_out);
  nand nand_6 (F, nand_5_out, nand_3_out);
endmodule

module _5 (
  input  X,
  input  Y,
  input  Z,
  output F
);

  wire nor_1_out, nor_2_out, nor_3_out, nor_4_out, nor_5_out;

  nor nor_1 (nor_1_out, X, X);
  nor nor_2 (nor_2_out, Y, Y);
  nor nor_3 (nor_3_out, nor_1_out, nor_2_out);
  nor nor_4 (nor_4_out, nor_3_out, nor_3_out);
  nor nor_5 (nor_5_out, Z, Z);
  nor nor_6 (F, nor_4_out, nor_5_out);
endmodule
