// Logisim project lab 5.circ as structural Verilog: 5 circuits, main circuit 1c
module _1c (
  input  A,
  input  B,
  input  C,
  output F
);

  wire xor_1_out;

  xor xor_1 (xor_1_out, B, C);
  xor xor_2 (F, A, xor_1_out);
endmodule

module _2c_isolated (
  input  A,
  input  B,
  input  C,
  input  D,
  input  A_2,
  input  B_2,
  input  D_2,
  input  A_3,
  input  B_3,
  input  C_2,
  input  D_3,
  output W,
  output X,
  output Y
);

  wire and_1_out, and_2_out, and_3_out, and_4_out, and_5_out, not_1_out, not_2_out, not_3_out, not_4_out,
       not_5_out, not_6_out, not_7_out, not_8_out, not_9_out, not_10_out;

  not not_1 (not_1_out, A);
  not not_2 (not_2_out, B);
  not not_3 (not_3_out, C);
  not not_4 (not_4_out, D);
  not not_5 (not_5_out, A_2);
  not not_6 (not_6_out, D_2);
  not not_7 (not_7_out, B_2);
  not not_8 (not_8_out, A_3);
  not not_9 (not_9_out, B_3);
  not not_10 (not_10_out, D_3);
  and and_1 (and_1_out, not_1_out, D);
  and and_2 (and_2_out, A, not_2_out, not_4_out);
  and and_3 (and_3_out, A, not_3_out, not_4_out);
  and and_4 (and_4_out, not_5_out, B_2, not_6_out);
  and and_5 (and_5_out, A_2, not_7_out, D_2);
  or or_1 (X, and_4_out, and_5_out);
  and and_6 (Y, not_8_out, not_9_out, C_2, not_10_out);
  or or_2 (W, and_1_out, and_2_out, and_3_out);
endmodule

module _2c_alt (
  input  A,
  input  B,
  input  C,
  input  D,
  output W,
  output X,
  output Y
);

  wire and_1_out, and_2_out, and_3_out, and_4_out, and_5_out, and_6_out, not_1_out, not_2_out, not_3_out,
       not_4_out, not_5_out, not_6_out, not_7_out, not_8_out, not_9_out, not_10_out, not_11_out, not_12_out;

  not not_1 (not_1_out, A);
  and and_1 (and_1_out, not_1_out, D);
  not not_2 (not_2_out, B);
  and and_2 (and_2_out, not_2_out, A, not_3_out);
  not not_3 (not_3_out, D);
  not not_4 (not_4_out, C);
  and and_3 (and_3_out, A, not_4_out, not_5_out);
  not not_5 (not_5_out, D);
  not not_6 (not_6_out, A);
  and and_4 (and_4_out, not_6_out, B, not_7_out);
  not not_7 (not_7_out, D);
  and and_5 (and_5_out, A, not_8_out, D);
  not not_8 (not_8_out, B);
  and and_6 (and_6_out, A, not_9_out, D);
  not not_9 (not_9_out, C);
  not not_10 (not_10_out, A);
  not not_11 (not_11_out, B);
  not not_12 (not_12_out, D);
  or or_1 (W, and_1_out, and_2_out, and_3_out);
  or or_2 (X, and_4_out, and_5_out, and_6_out);
  and and_7 (Y, not_10_out, not_11_out, C, not_12_out);
endmodule

module _3c (
  input  A1,
  input  A0,
  input  B1,
  input  B0,
  output F,
  output G
);

  wire and_1_out, and_2_out, and_3_out, and_4_out, and_5_out, and_6_out, not_1_out, not_2_out, not_3_out,
       not_4_out, not_5_out, not_6_out, not_7_out, not_8_out;

  not not_1 (not_1_out, B1);
  and and_1 (and_1_out, A0, not_1_out, not_2_out);
  not not_2 (not_2_out, B0);
  and and_2 (and_2_out, A1, not_3_out);
  not not_3 (not_3_out, B1);
  and and_3 (and_3_out, A1, A0, not_4_out);
  not not_4 (not_4_out, B0);
  not not_5 (not_5_out, A1);
  not not_6 (not_6_out, A0);
  and and_4 (and_4_out, not_5_out, not_6_out, B0);
  not not_7 (not_7_out, A1);
  and and_5 (and_5_out, not_7_out, B1);
  not not_8 (not_8_out, A0);
  and and_6 (and_6_out, not_8_out, B1, B0);
  or or_1 (F, and_1_out, and_2_out, and_3_out);
  or or_2 (G, and_4_out, and_5_out, and_6_out);
endmodule

module _4c (
  input  A,
  input  B,
  input  C,
  input  D,
  output F
);

  wire and_1_out, not_1_out, not_2_out, not_3_out;

  not not_1 (not_1_out, A);
  not not_2 (not_2_out, B);
  not not_3 (not_3_out, C);
  and and_1 (and_1_out, not_1_out, not_2_out, not_3_out);
  or or_1 (F, and_1_out, D);
endmodule
