// Logisim project lab 6.circ as structural Verilog: 5 circuits, main circuit 1a
module _1a (
  input  X,
  input  Y,
  input  Z,
  output F
);

  wire and_1_out, and_2_out, and_3_out, not_1_out, not_2_out, not_3_out, not_4_out;

  not not_1 (not_1_out, X);
  not not_2 (not_2_out, Y);
  not not_3 (not_3_out, Y);
  not not_4 (not_4_out, Z);
  and and_1 (and_1_out, not_1_out, not_2_out);
  and and_2 (and_2_out, not_3_out, not_4_out);
  and and_3 (and_3_out, X, Z, Y);
  or or_1 (F, and_1_out, and_2_out, and_3_out);
endmodule

module _1b (
  input  X,
  input  Y,
  input  Z,
  input  W,
  output G
);

  wire and_1_out, and_2_out, and_3_out, not_1_out, not_2_out, not_3_out, not_4_out;

  not not_1 (not_1_out, X);
  and and_1 (and_1_out, not_1_out, not_2_out);
  not not_2 (not_2_out, Y);
  not not_3 (not_3_out, X);
  and and_2 (and_2_out, not_3_out, not_4_out, W);
  not not_4 (not_4_out, Z);
  and and_3 (and_3_out, Y, X, W);
  or or_1 (G, and_1_out, and_2_out, and_3_out);
endmodule

module _2c (
  input  A,
  input  B,
  input  C,
  input  D,
  output W,
  output X,
  output Y,
  output Z
);

  wire not_1_out, not_2_out, not_3_out;

  not not_1 (not_1_out, A);
  and and_1 (W, not_1_out, not_2_out, not_3_out);
  not not_2 (not_2_out, B);
  not not_3 (not_3_out, C);
  xor xor_1 (X, B, C);
  not not_4 (Z, D);

  assign Y = C;
endmodule

module _3c (
  input  X,
  input  Y,
  input  Z,
  input  W,
  output A,
  output B,
  output C,
  output D
);

  wire and_1_out, and_2_out, and_3_out, and_4_out, and_5_out, and_6_out, not_1_out, not_2_out, not_3_out,
       not_4_out, not_5_out, not_6_out;

  and and_1 (and_1_out, Y, Z, not_1_out);
  not not_1 (not_1_out, W);
  not not_2 (not_2_out, Y);
  and and_2 (and_2_out, not_2_out, Z, not_3_out);
  not not_3 (not_3_out, W);
  and and_3 (and_3_out, Y, not_4_out);
  not not_4 (not_4_out, Z);
  and and_4 (and_4_out, Y, W);
  not not_5 (not_5_out, Z);
  and and_5 (and_5_out, not_5_out, not_6_out);
  not not_6 (not_6_out, W);
  and and_6 (and_6_out, Z, W);
  not not_7 (D, W);
  or or_1 (A, X, and_1_out);
  or or_2 (B, and_2_out, and_3_out, and_4_out);
  or or_3 (C, and_5_out, and_6_out);
endmodule

module _4c (
  input  A,
  input  B,
  input  C,
  output U,
  output V,
  output W,
  output X,
  output Y,
  output Z
);

  wire and_2_out, and_3_out, and_4_out, and_5_out, not_1_out, not_2_out, not_3_out, not_4_out;

  and and_1 (U, A, B);
  not not_1 (not_1_out, B);
  not not_2 (not_2_out, A);
  not not_3 (not_3_out, B);
  not not_4 (not_4_out, C);
  and and_2 (and_2_out, A, not_1_out);
  and and_3 (and_3_out, A, C);
  and and_4 (and_4_out, not_2_out, B, C);
  and and_5 (and_5_out, A, not_3_out, C);
  and and_6 (X, B, not_4_out);
  or or_1 (V, and_2_out, and_3_out);
  or or_2 (W, and_4_out, and_5_out);

  assign Y = 1'b0;
  assign Z = C;
endmodule
