// Logisim project lab 7.circ as structural Verilog: 6 circuits, main circuit 1a
module _1a (
  input  S,
  input  I0,
  input  I1,
  output Y
);

  wire and_1_out, and_2_out, not_1_out;

  not not_1 (not_1_out, S);
  and and_1 (and_1_out, not_1_out, I0);
  and and_2 (and_2_out, S, I1);
  or or_1 (Y, and_1_out, and_2_out);
endmodule

module _1b (
  input  I0,
  input  I1,
  input  S1,
  input  S0,
  input  I2,
  input  I3,
  output Y
);

  wire and_1_out, and_2_out, and_3_out, and_4_out, and_5_out, and_6_out, not_1_out, not_2_out, not_3_out,
       or_1_out, or_2_out;

  not not_1 (not_1_out, S0);
  and and_1 (and_1_out, not_1_out, I0);
  and and_2 (and_2_out, S0, I1);
  not not_2 (not_2_out, S0);
  and and_3 (and_3_out, not_2_out, I2);
  and and_4 (and_4_out, S0, I3);
  or or_1 (or_1_out, and_1_out, and_2_out);
  or or_2 (or_2_out, and_3_out, and_4_out);
  not not_3 (not_3_out, S1);
  and and_5 (and_5_out, not_3_out, or_1_out);
  and and_6 (and_6_out, S1, or_2_out);
  or or_3 (Y, and_5_out, and_6_out);
endmodule

module _2 (
  input  X,
  input  Y,
  input  Z,
  output F
);

  wire not_1_out;

  not not_1 (not_1_out, Z);
  Multiplexer #(.select(2)) multiplexer_1 (
    .in0(not_1_out), .in1(1'b1), .in2(Z), .in3(1'b0), .out(F), .sel({X, Y}));  // open: en
endmodule

module _3 (
  input  A,
  input  B,
  input  S2,
  input  S1,
  input  S0,
  output F
);

  wire and_1_out, not_1_out, not_2_out, not_3_out, or_1_out, xor_1_out;

  xor xor_1 (xor_1_out, A, B);
  and and_1 (and_1_out, A, B);
  or or_1 (or_1_out, A, B);
  not not_1 (not_1_out, A);
  not not_2 (not_2_out, B);
  Multiplexer #(.select(3)) multiplexer_1 (
    .in0(A), .in1(not_1_out), .in2(B), .in3(not_2_out), .in4(xor_1_out), .in5(not_3_out), .in6(or_1_out),
    .in7(and_1_out), .out(F), .sel({S2, S1, S0}));  // open: en
  not not_3 (not_3_out, xor_1_out);
endmodule

module _4 (
  input  E,
  input  I1,
  input  I0,
  output D0,
  output D1,
  output D2,
  output D3
);

  wire nor_1_out, nor_2_out, nor_3_out, nor_4_out, nor_5_out, nor_6_out, nor_7_out, nor_8_out;

  nor nor_1 (nor_1_out, E, E);
  nor nor_2 (nor_2_out, I0, I0);
  nor nor_3 (nor_3_out, E, E);
  nor nor_4 (nor_4_out, I1, I1);
  nor nor_5 (nor_5_out, E, E);
  nor nor_6 (nor_6_out, I1, I1);
  nor nor_7 (nor_7_out, E, E);
  nor nor_8 (nor_8_out, I0, I0);
  nor nor_9 (D0, I1, I0, nor_1_out);
  nor nor_10 (D1, nor_2_out, I1, nor_3_out);
  nor nor_11 (D2, nor_4_out, I0, nor_5_out);
  nor nor_12 (D3, nor_6_out, nor_7_out, nor_8_out);
endmodule

module _5 (
  input  [1:0] I1_I0,
  input  I2,
  output D0,
  output D1,
  output D2,
  output D3,
  output D4,
  output D5,
  output D6,
  output D7
);

  wire not_1_out;

  not not_1 (not_1_out, I2);
  Decoder #(.select(2)) decoder_1 (.out0(D0), .out1(D1), .out2(D2), .out3(D3), .sel(I1_I0), .en(not_1_out));
  Decoder #(.select(2)) decoder_2 (.out0(D4), .out1(D5), .out2(D6), .out3(D7), .sel(I1_I0), .en(I2));
endmodule
