// Logisim project lab 8.circ as structural Verilog: 3 circuits, main circuit 1c
module _1c (
  input  A,
  input  B,
  input  Bin,
  output D,
  output Bout
);

  wire and_1_out, and_2_out, and_3_out, not_1_out, xor_1_out;

  not not_1 (not_1_out, A);
  xor xor_1 (xor_1_out, A, B);
  and and_1 (and_1_out, not_1_out, B);
  and and_2 (and_2_out, not_1_out, Bin);
  and and_3 (and_3_out, B, Bin);
  or or_1 (Bout, and_1_out, and_2_out, and_3_out);
  xor xor_2 (D, xor_1_out, Bin);
endmodule

module _2_p1 (
  input  M,
  input  [3:0] A,
  input  [3:0] B,
  output [3:0] S,
  output Cout
);

  wire adder_1_cout, adder_2_cout, adder_3_cout, xor_1_out, xor_2_out, xor_3_out, xor_4_out;

  xor xor_1 (xor_1_out, B[0], M);
  xor xor_2 (xor_2_out, B[1], M);
  xor xor_3 (xor_3_out, B[2], M);
  xor xor_4 (xor_4_out, B[3], M);
  Adder #(.width(1)) adder_1 (.a(A[0]), .b(xor_1_out), .out(S[0]), .cin(M), .cout(adder_1_cout));
  Adder #(.width(1)) adder_2 (.a(A[1]), .b(xor_2_out), .out(S[1]), .cin(adder_1_cout), .cout(adder_2_cout));
  Adder #(.width(1)) adder_3 (.a(A[2]), .b(xor_3_out), .out(S[2]), .cin(adder_2_cout), .cout(adder_3_cout));
  Adder #(.width(1)) adder_4 (.a(A[3]), .b(xor_4_out), .out(S[3]), .cin(adder_3_cout), .cout(Cout));
endmodule

module _2p2_real (
  input  M,
  input  [3:0] A,
  input  [3:0] B,
  input  [3:0] in_4,
  output a_2,
  output b_2,
  output c,
  output d,
  output e,
  output f,
  output g
);

  wire and_1_out, comparator_1_gt;
  wire [2:2] comparator_2_gt;
  wire [3:0] adder_1_out, n2_p1_1_s, n2_p1_2_s;

  _2_p1 u_2_p1_1 (.M(M), .A(A), .B(B), .S(n2_p1_1_s));  // open: Cout
  Comparator #(.width(4), .mode("unsigned")) comparator_1 (.a(B), .b(A), .gt(comparator_1_gt));  // open: eq, lt
  not not_1 (a_2, and_1_out);
  _2_p1 u_2_p1_2 (.M(M), .A(in_4), .B(n2_p1_1_s), .S(n2_p1_2_s));  // open: Cout
  and and_1 (and_1_out, comparator_1_gt, M);
  not not_2 (d, and_1_out);
  _7_Segment_Display u_7_segment_display_1 (.g(1'b0), .f(d), .a(a_2), .b(1'b1), .e(e), .d(d), .c(1'b1));  // open: dp
  not not_3 (e, and_1_out);
  not not_4 (d, and_1_out);
  Comparator #(.width(4), .mode("unsigned")) comparator_2 (
    .a(n2_p1_2_s), .b(4'b1001), .gt(comparator_2_gt[2]));  // open: eq, lt
  Hex_Digit_Display hex_digit_display_1 (.value({3'b000, comparator_2_gt[2]}));  // open: dp
  Hex_Digit_Display hex_digit_display_2 (.value(adder_1_out));  // open: dp
  Adder #(.width(4)) adder_1 (
    .a(n2_p1_2_s), .b({1'b0, {2{comparator_2_gt[2]}}, 1'b0}), .out(adder_1_out), .cin(1'b0));  // open: cout

  assign b_2 = 1'b1;
  assign c = 1'b1;
  assign f = d;
  assign g = 1'b0;
endmodule
