// Logisim project lab 9.circ as structural Verilog: 5 circuits, main circuit 1b
module _1b (
  input  T,
  output Q,
  output Q_prime
);

  wire clock_1_out, xor_1_out;

  xor xor_1 (xor_1_out, Q, T);
  Clock clock_1 (.out(clock_1_out));
  D_Flip_Flop d_ff_1 (.clk(clock_1_out), .D(xor_1_out), .Q(Q), .Qn(Q_prime));  // open: preset, en, reset
endmodule

module _2b (
  input  J,
  input  K,
  output Q,
  output Q_prime
);

  wire and_1_out, and_2_out, clock_1_out, not_1_out, or_1_out;

  and and_1 (and_1_out, Q_prime, J);
  not not_1 (not_1_out, K);
  and and_2 (and_2_out, not_1_out, Q);
  Clock clock_1 (.out(clock_1_out));
  or or_1 (or_1_out, and_1_out, and_2_out);
  D_Flip_Flop d_ff_1 (.clk(clock_1_out), .D(or_1_out), .Q(Q), .Qn(Q_prime));  // open: preset, en, reset
endmodule

module _3 (
  output QA,
  output QB,
  output QC,
  output QA_prime,
  output QB_prime,
  output QC_prime
);

  wire clock_1_out, not_1_out, or_1_out;

  Clock clock_1 (.out(clock_1_out));
  J_K_Flip_Flop j_k_ff_1 (.J(QB), .clk(clock_1_out), .K(QB), .Q(QA), .Qn(QA_prime));  // open: preset, en, reset
  or or_1 (or_1_out, QC, QA);
  J_K_Flip_Flop j_k_ff_2 (.J(or_1_out), .clk(clock_1_out), .K(1'b1), .Q(QB), .Qn(QB_prime));  // open: preset, en, reset
  not not_1 (not_1_out, QB);
  J_K_Flip_Flop j_k_ff_3 (
    .J(not_1_out), .clk(clock_1_out), .K(1'b1), .Q(QC), .Qn(QC_prime));  // open: preset, en, reset
endmodule

module _4 (
  input  G,
  input  L,
  output Q,
  output Q_prime
);

  wire and_1_out, and_2_out, clock_1_out, not_1_out;

  and and_1 (and_1_out, G, L);
  Clock clock_1 (.out(clock_1_out));
  and and_2 (and_2_out, G, not_1_out);
  not not_1 (not_1_out, L);
  J_K_Flip_Flop j_k_ff_1 (
    .J(and_1_out), .clk(clock_1_out), .K(and_2_out), .Q(Q), .Qn(Q_prime));  // open: preset, en, reset
endmodule

module _5 (
  output QA,
  output QB,
  output QC,
  output QD,
  output QA_prime,
  output QB_prime,
  output QC_prime,
  output QD_prime
);

  wire and_1_out, and_2_out, and_3_out, clock_1_out, not_1_out, not_2_out, not_3_out, or_1_out;

  Clock clock_1 (.out(clock_1_out));
  and and_1 (and_1_out, QB, QC);
  not not_1 (not_1_out, QC);
  J_K_Flip_Flop j_k_ff_1 (
    .J(and_1_out), .clk(clock_1_out), .K(not_1_out), .Q(QA), .Qn(QA_prime));  // open: preset, en, reset
  or or_1 (or_1_out, QC, QA);
  J_K_Flip_Flop j_k_ff_2 (.J(QD), .clk(clock_1_out), .K(or_1_out), .Q(QB), .Qn(QB_prime));  // open: preset, en, reset
  not not_2 (not_2_out, QB);
  and and_2 (and_2_out, not_2_out, QD);
  J_K_Flip_Flop j_k_ff_3 (
    .J(1'b1), .clk(clock_1_out), .K(and_2_out), .Q(QC), .Qn(QC_prime));  // open: preset, en, reset
  not not_3 (not_3_out, QC);
  and and_3 (and_3_out, not_3_out, QA);
  J_K_Flip_Flop j_k_ff_4 (
    .J(1'b1), .clk(clock_1_out), .K(and_3_out), .Q(QD), .Qn(QD_prime));  // open: preset, en, reset
endmodule
