// Logisim project midterm.circ as structural Verilog: 1 circuit, main circuit main
module main (
  input  A,
  input  B,
  input  C,
  input  D,
  output F,
  output G,
  output X
);

  wire and_1_out, and_2_out, and_3_out, and_4_out, and_5_out, nor_1_out, not_1_out, not_2_out, not_3_out,
       not_4_out;

  not not_1 (not_1_out, C);
  and and_1 (and_1_out, B, not_1_out, D);
  and and_2 (and_2_out, B, D, not_2_out);
  not not_2 (not_2_out, A);
  not not_3 (not_3_out, B);
  and and_3 (and_3_out, not_3_out, D, A);
  and and_4 (and_4_out, A, B);
  and and_5 (and_5_out, A, C);
  not not_4 (not_4_out, A);
  nor nor_1 (nor_1_out, B, C);
  or or_1 (F, and_1_out, and_2_out, and_3_out);
  or or_2 (G, and_4_out, and_5_out);
  or or_3 (X, not_4_out, nor_1_out);
endmodule
